# Fritzing sketch breadboard (saved by Fritzing 0.9.2b)
breadboards: 1

parts:
  WeMos_D1_Mini1 = WeMos D1 Mini
  U1 = Voltage Regulator [package=to220-adj]
  JACK1 = 2.1mm Barrel Jack with Terminal Block
  R1 = Resistor [tolerance=±5% resistance=330 package="0603 [SMD]"]
  R2 = Resistor [tolerance=±5% resistance=1k package="0603 [SMD]"]
  C1 = Ceramic Capacitor [capacitance="100 nF" package="0603 [SMD, multilayer]"]
  C2 = Electrolytic Capacitor [capacitance=1µF package="100 mil [THT, electrolytic]"]
  R3 = Resistor [tolerance=±5% resistance=5.6k package="0603 [SMD]"]
  R4 = Resistor [tolerance=±5% resistance=5.6k package="0603 [SMD]"]
  R5 = Resistor [tolerance=±5% resistance=8.2k package="0603 [SMD]"]
  R6 = PHOTOCELL [package=photocell]
  R7 = Resistor [tolerance=±5% resistance=8.2k package="0603 [SMD]"]

nets:
  N1: WeMos_D1_Mini1.3V3, R3.Pin_0, R4.Pin_0, R5.Pin_0, R6.P$1
  N2: WeMos_D1_Mini1.5V, U1.IN, R1.Pin_1, C2.+
  N3: WeMos_D1_Mini1.A0, R6.P$2, R7.Pin_0
  N4: WeMos_D1_Mini1.D1, R3.Pin_1
  N5: WeMos_D1_Mini1.D2, R4.Pin_1
  N6: WeMos_D1_Mini1.G, JACK1.NEG, R2.Pin_0, C1.1, C2.-, R7.Pin_1
  N7: U1.ADJ, R1.Pin_0, R2.Pin_1
  N8: U1.OUT, JACK1.POS, C1.0

notes:
  SCL
  SDA
  /reset
  10-15V

custom parts:
  WeMos D1 Mini: The D1 mini is a mini wifi board based on ESP-8266EX.
